# Fritzing sketch Sketch (saved by Fritzing 0.9.6b)

parts:
  A1 = Wemos S2 Mini [part_number="WeMos D1 Mini Lite"]
  M1 = fc-51 [package=THT]
  J1 = Basic Servo
  M2 = fc-51 [package=THT]
  M3 = fc-51 [package=THT]
  M4 = fc-51 [package=THT]
  YwRobot_Power_Supply1 = YwRobot Breadboard Power Supply [part_number=545043]
  M5 = fc-51 [package=THT]
  M6 = fc-51 [package=THT]

nets:
  N1: A1.Pin_2, M2.pin1
  N2: A1.Pin_3, J1.pulse
  N3: A1.Pin_4, M5.pin1
  N4: A1.Pin_9, M4.pin1
  N5: A1.Pin_10, M3.pin1
  N6: A1.Pin_11, M1.pin1
  N7: A1.Pin_12, M6.pin1
  N8: A1.Pin_17, YwRobot_Power_Supply1.VCC#6
  N9: A1.Pin_18, A1.Pin_26, YwRobot_Power_Supply1.GND#12
  N10: M1.pin2, J1.gnd, M2.pin2, M3.pin2, M4.pin2, YwRobot_Power_Supply1.GND#11
  N11: M1.pin3, J1.vcc, M2.pin3, M3.pin3, M4.pin3, YwRobot_Power_Supply1.VCC#5

custom parts:
  Wemos S2 Mini: A mini wifi board based on the ESP32-S2FN4R2.
  YwRobot Breadboard Power Supply: The YwRobot Breadboard Power Supply (MB-V2) has two power rails; they can be 5V or 3V3. Power to the module can be provided through the female USB socket or through the A10 (female) 2.1mm power jack.
